# Fritzing sketch STET002 (saved by Fritzing 0.9.3b)
circuit board: 4.70983cm x 4.63935cm

parts:
  Teensy_3_2 = female pin header, 14 pins [form="♀ (female)"]
  Teensy_Audio_Shield = female pin header, 14 pins [form="♀ (female)"]
  J3 = female pin header, 14 pins [form="♀ (female)"]
  J4 = female pin header, 14 pins [form="♀ (female)"]
  Micro_LiPo = female pin header, 4 pins [form="♀ (female)"]
  Bluetooth_Antenna = female pin header, 6 pins [form="♀ (female)"]
  Audio_L_G_G_R = female pin header, 4 pins [form="♀ (female)"]
  Headphone_Audio = longpad pin header, 3 pins [form="long pad"]

nets:
  N1: Teensy_3_2.pin1, Teensy_Audio_Shield.pin1, Micro_LiPo.pin2, Micro_LiPo.pin3, Bluetooth_Antenna.pin3
  N2: Teensy_3_2.pin2, Teensy_Audio_Shield.pin2, Bluetooth_Antenna.pin4
  N3: Teensy_3_2.pin3, Teensy_Audio_Shield.pin3, Bluetooth_Antenna.pin5
  N4: Teensy_3_2.pin4, Teensy_Audio_Shield.pin4
  N5: Teensy_3_2.pin5, Teensy_Audio_Shield.pin5
  N6: Teensy_3_2.pin6, Teensy_Audio_Shield.pin6
  N7: Teensy_3_2.pin7, Teensy_Audio_Shield.pin7
  N8: Teensy_3_2.pin8, Teensy_Audio_Shield.pin8
  N9: Teensy_3_2.pin9, Teensy_Audio_Shield.pin9
  N10: Teensy_3_2.pin10, Teensy_Audio_Shield.pin10
  N11: Teensy_3_2.pin11, Teensy_Audio_Shield.pin11
  N12: Teensy_3_2.pin12, Teensy_Audio_Shield.pin12
  N13: Teensy_3_2.pin13, Teensy_Audio_Shield.pin13
  N14: Teensy_3_2.pin14, Teensy_Audio_Shield.pin14
  N15: J3.pin1, J4.pin1, Micro_LiPo.pin1, Micro_LiPo.pin4, Bluetooth_Antenna.pin2
  N16: J3.pin2, J4.pin2
  N17: J3.pin3, J4.pin3
  N18: J3.pin4, J4.pin4
  N19: J3.pin5, J4.pin5
  N20: J3.pin6, J4.pin6
  N21: J3.pin7, J4.pin7
  N22: J3.pin8, J4.pin8
  N23: J3.pin9, J4.pin9
  N24: J3.pin10, J4.pin10
  N25: J3.pin11, J4.pin11
  N26: J3.pin12, J4.pin12
  N27: J3.pin13, J4.pin13
  N28: J3.pin14, J4.pin14
  N29: Audio_L_G_G_R.pin1, Headphone_Audio.pin3
  N30: Audio_L_G_G_R.pin2, Audio_L_G_G_R.pin3, Headphone_Audio.pin1
  N31: Audio_L_G_G_R.pin4, Headphone_Audio.pin2
